// Logisim project alu.circ as structural Verilog: 1 circuit, main circuit main
module main (
  input  [7:0] N,
  input  [7:0] R0,
  input  [7:0] R1,
  input  [3:0] FLAGS,
  input  [4:0] INST,
  output [7:0] ACC,
  output [7:0] ACC2,
  output [3:0] OSZC
);

  wire [3:0] multiplexer_1_out;
  wire [23:0] adc_1_out_2, add_1_out_2, cbw_1_xfa2a1, xchg_1_xfa2a1;

  XCHG xchg_1 (.XFR1R0N({4'b0000, FLAGS, R1, R0, N}), .XFA2A1(xchg_1_xfa2a1));
  CBW cbw_1 (.XFR1R0N({4'b0000, FLAGS, R1, R0, N}), .XFA2A1(cbw_1_xfa2a1));
  ADD add_1 (.in_1({4'b0000, FLAGS, R1, R0, N}), .out_2(add_1_out_2));
  ADC adc_1 (.in_1({4'b0000, FLAGS, R1, R0, N}), .out_2(adc_1_out_2));
  Multiplexer #(.select(5), .width(24)) multiplexer_1 (
    .in0(xchg_1_xfa2a1), .in1(cbw_1_xfa2a1), .in2(add_1_out_2), .in3(adc_1_out_2),
    .out({multiplexer_1_out, OSZC, ACC2, ACC}), .sel(INST));  // open: in4, in5, in6, in7, in8, in9, in10, in11, in12, in13, in14, in15, in16, in17, in18, in19, in20, in21, in22, in23, in24, in25, in26, in27, in28, in29, in30, in31
endmodule
